# Fritzing sketch circuito_kantam (saved by Fritzing 1.0.1rc)
breadboards: 1

parts:
  M1 = DOIT Esp32 DevKit v1 (30 pins long, 11 pins width) [part_number=ESP32S-PIN30]
  J1 = Basic Servo
  L298N2 = L298N DC motor driver
  BATT1 = 4xAA Switchable Battery Pack w/Bare Wire
  M2 = gear-motor
  M3 = gear-motor

nets:
  GND: M1.GND, J1.gnd, L298N2.GND, BATT1.NEG
  N1: M1.D32, L298N2.ENA
  N2: M1.D33, L298N2.IN1
  N3: M1.D25, L298N2.IN2
  N4: M1.D26, L298N2.ENB
  N5: M1.D27, L298N2.IN3
  N6: M1.D14, L298N2.IN4
  N7: M1.D13, J1.pulse
  VIN: M1.VIN, J1.vcc
  N8: L298N2.OUT1, M2.pin_2
  N9: L298N2.OUT2, M2.pin_1
  N10: L298N2.OUT3, M3.pin_2
  N11: L298N2.OUT4, M3.pin_1
  N12: L298N2.12V, BATT1.POS

custom parts:
  DOIT Esp32 DevKit v1 (30 pins long, 11 pins width): The DOIT Esp32 DevKit v1 is one of the development board created by DOIT to evaluate the ESP-WROOM-32 module. It is based on the ESP32 microcontroller that boasts Wifi, Bluetooth, Ethernet and Low Power support all in a single chip. (vanepp) made breadboard work, adjusted pin numbering and labels and reduced size of schematic and cleaned up pcb. This chip is 30pins long (2 x15) and 11 pins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
  L298N DC motor driver: 2x DC motor driver with 78M05 positive voltage regulator (7..35 V) L298N: max 46 V, 2 A Set 5 V Enable jumper to enable 5 V regultor (needed for the L298N) and +5 V output at screw terminal or supply external +5 V at screw terminal Set ENA and/or ENB to +5 V to enable motor permanently or supply ENA and/or ENB with PWM signal IN1 and IN2 set rotation directory for motor A (OUT1/OUT2) IN2 and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
  4xAA Switchable Battery Pack w/Bare Wire: 4xAA Switchable Battery Pack with Bare Wire connection
